# Fritzing sketch SMART-D (saved by Fritzing 0.9.3b)

parts:
  LCD1 = LCD screen  # not connected
  U2 = EM406 GPS Connector [package=em406]
  Part2 = Arduino Uno (Rev3)
  GSM_SIM_GPSR_SMS_SIM900_SIM2 = SIM800L [package=THT]
  hc-sr1 = hc-sr04
  U3 = LM2596 step down module
  VCC1 = 4 x AAA Battery Mount

nets:
  GND: U2.GND1, Part2.GND, GSM_SIM_GPSR_SMS_SIM900_SIM2.GND, hc-sr1.GND, U3.IN-, U3.OUT-
  VCC: U2.VCC, Part2.3V3
  N1: U2.RX, Part2.D10_PWM/SS
  N2: U2.TX, Part2.D11_PWM/MOSI
  N3: Part2.D8, hc-sr1.Echo
  N4: Part2.D9_PWM, hc-sr1.Trig
  N5: Part2.D6_PWM, GSM_SIM_GPSR_SMS_SIM900_SIM2.SIM_TXD
  N6: Part2.D7, GSM_SIM_GPSR_SMS_SIM900_SIM2.SIM_RXD
  N7: Part2.ioref, hc-sr1.VCC
  N8: Part2.VIN, U3.OUT+, VCC1.+
  N9: GSM_SIM_GPSR_SMS_SIM900_SIM2.5V, U3.IN+

custom parts:
  LM2596 step down module: LM2596 DC-DC step down power supply module 3 A.

// code stored in the sketch: SSS2.ino
#include "TinyGPS++.h"
#include "SoftwareSerial.h"

SoftwareSerial se
